// Logisim project Project02.circ as structural Verilog
module Half_Adder (
  input  a,
  input  b,
  output sum,
  output carry
);

  xor xor_1 (sum, a, b);
  and and_1 (carry, a, b);
endmodule

module Full_Adder (
  input  a,
  input  b,
  input  c,
  output sum,
  output carry
);

  wire and_1_out, and_2_out, xor_1_out;

  xor xor_1 (xor_1_out, a, b);
  and and_1 (and_1_out, a, b);
  xor xor_2 (sum, xor_1_out, c);
  and and_2 (and_2_out, xor_1_out, c);
  or or_1 (carry, and_2_out, and_1_out);
endmodule

module Add_4 (
  input  a0,
  input  a1,
  input  a2,
  input  a3,
  input  b0,
  input  b1,
  input  b2,
  input  b3,
  output out0,
  output out1,
  output out2,
  output out3
);

  wire adder_1_cout, adder_2_cout, adder_3_cout;

  Adder #(.width(1)) adder_1 (.a(a0), .b(b0), .out(out0), .cout(adder_1_cout));  // open: cin
  Adder #(.width(1)) adder_2 (.a(a1), .b(b1), .out(out1), .cin(adder_1_cout), .cout(adder_2_cout));
  Adder #(.width(1)) adder_3 (.a(a2), .b(b2), .out(out2), .cin(adder_2_cout), .cout(adder_3_cout));
  Adder #(.width(1)) adder_4 (.a(a3), .b(b3), .out(out3), .cin(adder_3_cout));  // open: cout
endmodule

module Inc4 (
  input  [15:0] a0,
  output [15:0] out0
);

  Adder #(.width(16)) adder_1 (.a(a0), .b(16'h1), .out(out0));  // open: cin, cout
endmodule
