// Logisim project Project03.circ as structural Verilog
module SR_Flip_Flop (
  input  Set,
  input  Reset,
  output Q,
  output notQ
);

  nand nand_1 (Q, Set, notQ);
  nand nand_2 (notQ, Q, Reset);
endmodule

module D_type_Flip_Flop (
  input  Set,
  input  Reset,
  output Q,
  output notQ
);

  wire nand_1_out, nand_2_out, not_1_out;

  not not_1 (not_1_out, Set);
  nand nand_1 (nand_1_out, Set, Reset);
  nand nand_2 (nand_2_out, Reset, not_1_out);
  nand nand_3 (Q, nand_1_out, notQ);
  nand nand_4 (notQ, Q, nand_2_out);
endmodule

module Bit (
  input  in,
  input  load,
  output out
);

  wire nand_1_out, nand_2_out, nand_4_out, not_1_out;

  not not_1 (not_1_out, in);
  nand nand_1 (nand_1_out, in, load);
  nand nand_2 (nand_2_out, load, not_1_out);
  nand nand_3 (out, nand_1_out, nand_4_out);
  nand nand_4 (nand_4_out, out, nand_2_out);
endmodule

module RAM8 (
  input  [15:0] in_1,
  input  load,
  input  [2:0] address,
  output [15:0] out_4
);

  wire clock_1_out, demultiplexer_1_out0, demultiplexer_1_out1, demultiplexer_1_out2, demultiplexer_1_out3,
       demultiplexer_1_out4, demultiplexer_1_out5, demultiplexer_1_out6, demultiplexer_1_out7;
  wire [15:0] register_1_q, register_2_q, register_3_q, register_4_q, register_5_q, register_6_q,
       register_7_q, register_8_q;

  Clock clock_1 (.out(clock_1_out));
  Demultiplexer #(.select(3), .enable("false")) demultiplexer_1 (
    .out0(demultiplexer_1_out0), .out1(demultiplexer_1_out1), .out2(demultiplexer_1_out2),
    .out3(demultiplexer_1_out3), .out4(demultiplexer_1_out4), .out5(demultiplexer_1_out5),
    .out6(demultiplexer_1_out6), .out7(demultiplexer_1_out7), .in(load), .sel(address));
  Register #(.width(16)) register_1 (
    .D(in_1), .en(demultiplexer_1_out0), .Q(register_1_q), .clk(clock_1_out));  // open: clr
  Register #(.width(16)) register_2 (
    .D(in_1), .en(demultiplexer_1_out2), .Q(register_2_q), .clk(clock_1_out));  // open: clr
  Register #(.width(16)) register_3 (
    .D(in_1), .en(demultiplexer_1_out1), .Q(register_3_q), .clk(clock_1_out));  // open: clr
  Register #(.width(16)) register_4 (
    .D(in_1), .en(demultiplexer_1_out3), .Q(register_4_q), .clk(clock_1_out));  // open: clr
  Register #(.width(16)) register_5 (
    .D(in_1), .en(demultiplexer_1_out4), .Q(register_5_q), .clk(clock_1_out));  // open: clr
  Register #(.width(16)) register_6 (
    .D(in_1), .en(demultiplexer_1_out5), .Q(register_6_q), .clk(clock_1_out));  // open: clr
  Register #(.width(16)) register_7 (
    .D(in_1), .en(demultiplexer_1_out6), .Q(register_7_q), .clk(clock_1_out));  // open: clr
  Register #(.width(16)) register_8 (
    .D(in_1), .en(demultiplexer_1_out7), .Q(register_8_q), .clk(clock_1_out));  // open: clr
  Multiplexer #(.select(3), .width(16)) multiplexer_1 (
    .in0(register_1_q), .in1(register_3_q), .in2(register_2_q), .in3(register_4_q), .in4(register_5_q),
    .in5(register_6_q), .in6(register_7_q), .in7(register_8_q), .out(out_4), .sel(address));  // open: en
endmodule
