// Logisim project mux.circ as structural Verilog: 12 circuits, main circuit Mux
module Not (
  input  a,
  output out_2
);

  nand nand_1 (out_2, a, a);
endmodule

module Mux (
  input  a,
  input  sel,
  input  b,
  output out
);

  wire nandA_out, nandB_out, notSel_out;

  nand notSel (notSel_out, sel, sel);
  nand nandA (nandA_out, a, notSel_out);
  nand nandB (nandB_out, sel, b);
  nand nandC (out, nandA_out, nandB_out);
endmodule

module DMux (
  input  in,
  input  sel,
  output a,
  output b
);

  wire notSel_out;

  not notSel (notSel_out, sel);
  and andA (b, in, sel);
  and andB (a, in, notSel_out);
endmodule

module Or (
  input  b,
  input  a,
  output out
);

  wire nand_1_out, nand_2_out;

  nand nand_1 (nand_1_out, b, b);
  nand nand_2 (nand_2_out, a, a);
  nand nand_3 (out, nand_1_out, nand_2_out);
endmodule

module Xor (
  input  a,
  input  b,
  output out
);

  wire nand_1_out, nand_2_out, nand_3_out;

  nand nand_1 (nand_1_out, a, b);
  nand nand_2 (nand_2_out, a, nand_1_out);
  nand nand_3 (nand_3_out, nand_1_out, b);
  nand nand_4 (out, nand_2_out, nand_3_out);
endmodule

module And (
  input  a,
  input  b,
  output out
);

  wire nand_1_out;

  nand nand_1 (nand_1_out, a, b);
  nand nand_2 (out, nand_1_out, nand_1_out);
endmodule

module Not16 (
  input  [15:0] a,
  output [15:0] out
);

  assign out = ~a;  // NOT_Gate not_1, 16 bits wide
endmodule

module Mux16 (
  input  [15:0] a,
  input  [15:0] b,
  input  sel,
  output [15:0] out
);

  Multiplexer #(.width(16), .enable("false")) multiplexer_1 (.in0(a), .in1(b), .out(out), .sel(sel));
endmodule

module And16 (
  input  [15:0] a,
  input  [15:0] b,
  output [15:0] out
);

  assign out = a & b;  // AND_Gate and_1, 16 bits wide
endmodule

module Or16 (
  input  [15:0] a,
  input  [15:0] b,
  output [15:0] out
);

  assign out = a | b;  // OR_Gate or_1, 16 bits wide
endmodule

module Or8Way (
  input  in_7,
  input  in_6,
  input  in_5,
  input  in_4,
  input  in_3,
  input  in_2,
  input  in_1,
  input  in_0,
  output out
);

  wire orA_out, orB_out, orC_out, orD_out, orE_out, orF_out;

  or orB (orB_out, in_2, orA_out);
  or orA (orA_out, in_1, in_0);
  or orD (orD_out, in_4, orC_out);
  or orC (orC_out, in_3, orB_out);
  or orF (orF_out, in_6, orE_out);
  or orE (orE_out, in_5, orD_out);
  or u_out (out, in_7, orF_out);
endmodule

module Mux4Way16 (
  input  [15:0] a_16,
  input  [15:0] b_16,
  input  [15:0] c_16,
  input  [15:0] d_16,
  input  sel_0,
  input  sel_1,
  output [15:0] out_16
);

  wire and_1_out;
  wire [15:0] multiplexer_1_out, multiplexer_2_out;

  Multiplexer #(.width(16), .enable("false")) multiplexer_1 (
    .in0(a_16), .in1(b_16), .out(multiplexer_1_out), .sel(sel_0));
  Multiplexer #(.width(16), .enable("false")) multiplexer_2 (
    .in0(c_16), .in1(d_16), .out(multiplexer_2_out), .sel(and_1_out));
  and and_1 (and_1_out, sel_1, sel_0);
  Multiplexer #(.width(16), .enable("false")) multiplexer_3 (
    .in0(multiplexer_1_out), .in1(multiplexer_2_out), .out(out_16), .sel(sel_1));
endmodule
